// Digital circuit core.dig as structural Verilog
module core (
  input  clk,
  output [31:0] out
);

  wire A, alu, alu_op, AluASrc, and_1_out, B, demultiplexer_1_out_1, imm, need_imm, r1Data, r2Data;
  wire [2:0] funct3;
  wire [4:0] rd, rs1, rs2;
  wire [6:0] funct7, opcode;
  wire [31:0] pc_1_out, sum_s;

  PC pc_1 (.in(sum_s), .clk(clk), .out(pc_1_out));
  Add #(.Bits(32)) sum (.a(pc_1_out), .b(32'h4), .c_i(1'b0), .s(sum_s));  // open: c_o
  Insts_Memory insts_memory_1 (.pc(pc_1_out), .out({funct7, rs2, rs1, funct3, rd, opcode}));
  // control_unit control_unit_1: pin names not known; wires that end beside it: opcode, funct3, funct7, r1Data, r2Data, alu_op, alu, need_imm
  register_unit register_unit_1 (
    .rdData({32{1'b0}}), .rs1(rs1), .rs2(rs2), .rd(rd), .clk(clk), .enable(1'b0));  // open: rs1Data, rs2Data
  // ImmGenerator immgenerator_1: pin names not known; wires that end beside it: {funct7, rs2, rs1, funct3, rd}, imm
  Demultiplexer demultiplexer_1 (.sel(alu), .in(1'b1), .out_1(demultiplexer_1_out_1));  // open: out_0
  and and_1 (and_1_out, need_imm, demultiplexer_1_out_1);
  Multiplexer multiplexer_1 (.sel(AluASrc), .in_0(r1Data), .in_1(opcode[0]), .out(A));
  Multiplexer multiplexer_2 (.sel(and_1_out), .in_0(r2Data), .in_1(imm), .out(B));
  // ALU alu_1: pin names not known; wires that end beside it: A, B, alu_op, out
  // Pins of 1 and 32 bits meet at {funct7, rs2, rs1, funct3, rd, opcode}
endmodule
